// Logisim project Logisim Design.circ as structural Verilog
module ALU (
  input  [15:0] Input,
  input  [15:0] Input_2,
  input  [1:0] ALU_Control_Signal,
  output Zero_Signal__for_branching,
  output [15:0] Output
);

  wire [15:0] adder_1_out, and_1_out, or_1_out, subtractor_1_out;

  Adder #(.width(16)) adder_1 (.a(Input), .b(Input_2), .out(adder_1_out));  // open: cin, cout
  Subtractor #(.width(16)) subtractor_1 (.a(Input), .b(Input_2), .out(subtractor_1_out));  // open: bin, bout
  assign and_1_out = Input & Input_2;  // AND_Gate and_1, 16 bits wide
  assign or_1_out = Input | Input_2;  // OR_Gate or_1, 16 bits wide
  Multiplexer #(.select(2), .width(16), .enable("false")) multiplexer_1 (
    .in0(adder_1_out), .in1(subtractor_1_out), .in2(and_1_out), .in3(or_1_out), .out(Output),
    .sel(ALU_Control_Signal));
  nor nor_1 (Zero_Signal__for_branching, Output[15], Output[14], Output[13], Output[12], Output[11], Output[10], Output[9], Output[8], Output[7], Output[6], Output[5], Output[4], Output[3], Output[2], Output[1], Output[0]);
endmodule

module Main_Control (
  input  [1:0] Operation_Code
);

  wire ALU_Source_out, beq_out, Extension_Operation_out, Load__lw_out, not_1_out, not_2_out, not_3_out,
       not_4_out, R_Formats_out, Register_Write_out, Store__sw_out;

  not not_1 (not_1_out, Operation_Code[0]);
  not not_2 (not_2_out, Operation_Code[1]);
  not not_3 (not_3_out, Operation_Code[1]);
  not not_4 (not_4_out, Operation_Code[0]);
  and R_Formats (R_Formats_out, not_1_out, not_2_out);
  and Load__lw (Load__lw_out, Operation_Code[0], not_3_out);
  and Store__sw (Store__sw_out, not_4_out, Operation_Code[1]);
  and beq (beq_out, Operation_Code[0], Operation_Code[1]);
  or Register_Write (Register_Write_out, R_Formats_out, Load__lw_out);
  or ALU_Source (ALU_Source_out, Load__lw_out, Store__sw_out);
  or Extension_Operation (Extension_Operation_out, Load__lw_out, Store__sw_out, beq_out);

  // Notes on the sheet:
  //   Register Destination
  //   Memory to Register
  //   Memoty Write
  //   Branch
  //   Memory Read
  //   ALUopt<1>
  //   ALUopt<0>
endmodule

module ALU_Control (
  input  [4:0] Function_Code,
  input  [1:0] ALUopt,
  output [1:0] ALU_Control_Signal
);

  Multiplexer #(.width(2), .enable("false")) multiplexer_1 (
    .in0(ALUopt), .in1(Function_Code[1:0]), .out(ALU_Control_Signal), .sel(ALUopt[1]));
endmodule
